# Fritzing sketch project-5-breadboard (saved by Fritzing 1.0.4)
breadboards: 1

parts:
  µC1 = ATmega32 [package=dip]
  LED1 = RGB LED (com. cathode, rgb) [color="Red (633nm)" current=0.030A package="5 mm [THT]"]
  LED3 = smd LED [color="Yellow (585nm)" package="0603 [SMD]"]
  LED4 = smd LED [color="Red (633nm)" package="0603 [SMD]"]
  LED5 = smd LED [color="Green (565nm)" package="0603 [SMD]"]
  R9 = Resistor Mini [tolerance=±5% resistance=220 package=THT]
  R10 = Resistor Mini [tolerance=±5% resistance=220 package=THT]
  R11 = Resistor Mini [tolerance=±5% resistance=220 package=THT]
  R12 = Resistor Mini [tolerance=±5% resistance=220 package=THT]
  R13 = Resistor Mini [tolerance=±5% resistance=220 package=THT]
  R14 = Resistor Mini [tolerance=±5% resistance=220 package=THT]
  PART2 = Sound Detector
  C1 = Tantalum Capacitor [capacitance=1μF voltage=35V package="100 mil [THT, tantalum]"]
  C2 = Tantalum Capacitor [capacitance=1μF voltage=35V package="100 mil [THT, tantalum]"]
  VCC1 = Battery block 9V [internal_resistance=0.1Ω]
  Capacitor1 = Tantalum Capacitor [capacitance=0.1µF voltage=35V package="C 6032 [SMD, tantalum]"]
  U2 = Voltage Regulator - Variable [package="TO220 [THT]"]

nets:
  N1: µC1.PB0, LED1.red_anode, R9.Pin_0, R9.Pin_1
  N2: µC1.PB2, LED1.green_anode, R10.Pin_0, R10.Pin_1
  N3: µC1.PB3, LED1.blue_anode, R11.Pin_0, R11.Pin_1
  VCC: µC1.VCC, µC1.AVCC, PART2.VCC, C1.+, Capacitor1.+, U2.ADJ
  GND1: µC1.GND1, µC1.GND2, LED1.common_cathode, R12.Pin_0, R13.Pin_0, R14.Pin_0, PART2.GND, C1.-, C2.-, VCC1.-, Capacitor1.-, U2.OUT
  N4: µC1.PD1, LED5.anode
  N5: µC1.PD2, LED5.cathode, R14.Pin_1
  N6: µC1.PD3, LED3.anode
  N7: µC1.PD4, LED3.cathode, R13.Pin_1
  N8: µC1.PD5, LED4.anode
  N9: µC1.PD6, LED4.cathode, R12.Pin_1
  N10: µC1.AREF, C2.+
  N11: µC1.PA0, PART2.ENVELOPE
  N12: VCC1.+, U2.IN

custom parts:
  ATmega32: AVR 8-bit microcontroller.
  Resistor Mini: A generic resistor (0.25W)
  Sound Detector: Electret microphone with multiple outputs. - First output is the actual audio - Second output is the amplitude envelope - Third output is a binary "sound present" indication - high while sound is present, low otherwise. Visit sparkfun.com for more documentations.
